# Fritzing sketch servopot (saved by Fritzing 0.7.10b)
breadboards: 1

parts:
  R1 = Rotary Potentiometer (Small) [maximum_resistance=100kΩ]
  Netduino1 = Netduino
  J1 = Basic Servo

nets:
  N1: R1.leg1, Netduino1.3V3
  N2: R1.wiper, Netduino1.A0
  GND: R1.leg2, Netduino1.GND, J1.gnd
  N3: Netduino1.D9_PWM2, J1.pulse
  +5V: Netduino1.+5V, J1.vcc

notes:
  10k Potentiometer
